// Logisim project logic.circ as structural Verilog: 2 circuits, main circuit FA
module FA (
  input  a,
  input  b,
  input  cin,
  output s,
  output cout
);

  wire and_1_out, and_2_out, and_3_out, and_4_out, and_5_out, and_6_out, and_7_out, not_1_out, not_2_out,
       not_3_out, not_4_out, not_5_out, not_6_out;

  not not_1 (not_1_out, a);
  not not_2 (not_2_out, b);
  not not_3 (not_3_out, a);
  not not_4 (not_4_out, cin);
  not not_5 (not_5_out, b);
  not not_6 (not_6_out, cin);
  and and_1 (and_1_out, b, cin);
  and and_2 (and_2_out, a, cin);
  and and_3 (and_3_out, a, b);
  and and_4 (and_4_out, not_1_out, not_2_out, cin);
  and and_5 (and_5_out, not_3_out, b, not_4_out);
  and and_6 (and_6_out, a, not_5_out, not_6_out);
  and and_7 (and_7_out, a, b, cin);
  or or_1 (cout, and_1_out, and_2_out, and_3_out);
  or or_2 (s, and_4_out, and_5_out, and_6_out, and_7_out);
endmodule

module MAIN (
  input  in_1,
  input  [3:0] in_2,
  input  in_3,
  input  [3:0] in_4,
  output [3:0] out_5,
  output out_6
);

  wire fa_1_cout, fa_2_cout, fa_3_cout, xor_1_out, xor_2_out, xor_3_out, xor_4_out;

  // Probe on in_2
  // Probe on in_4
  xor xor_1 (xor_1_out, in_3, in_4[0]);
  FA fa_1 (.a(in_2[0]), .b(xor_1_out), .cin(in_1), .s(out_5[0]), .cout(fa_1_cout));
  xor xor_2 (xor_2_out, in_3, in_4[1]);
  FA fa_2 (.a(in_2[1]), .b(xor_2_out), .cin(fa_1_cout), .s(out_5[1]), .cout(fa_2_cout));
  xor xor_3 (xor_3_out, in_3, in_4[2]);
  FA fa_3 (.a(in_2[2]), .b(xor_3_out), .cin(fa_2_cout), .s(out_5[2]), .cout(fa_3_cout));
  xor xor_4 (xor_4_out, in_3, in_4[3]);
  FA fa_4 (.a(in_2[3]), .b(xor_4_out), .cin(fa_3_cout), .s(out_5[3]), .cout(out_6));
  // Probe on out_5
endmodule
